// Logisim project exp1-3 ˫�ؿ��� - ������.circ as structural Verilog: 2 circuits, main circuit main
module main (
  output A,
  output B,
  output C,
  output Y,
  output halt
);

  wire clock_1_out;

  Counter #(.width(3), .max('h7)) counter_1 (
    .Q({C, B, A}), .carry(halt), .clk(clock_1_out));  // open: load, D, count, clr
  Clock clock_1 (.out(clock_1_out));
  vote vote_1 (.A(A), .B(B), .Y(Y), .C(C));
  LED led_1 (.in(Y));

  // Notes on the sheet:
  //   顶层模块与自制子模块连接部分
  //   本地Logisim验证区域
  //   按Control+K触发执行，再次按Control+K暂停触发
endmodule

module vote (
  input  A,
  input  B,
  input  C,
  output Y
);

  wire and_1_out, and_2_out, and_3_out;

  and and_1 (and_1_out, A, C);
  and and_2 (and_2_out, B, A);
  and and_3 (and_3_out, C, B);
  or or_1 (Y, and_2_out, and_1_out, and_3_out);

  // Notes on the sheet:
  //   自制子模块实现区域
endmodule
