// Logisim project exp3-1 D触发器 - 作答区.circ as structural Verilog: 3 circuits, main circuit main
module main (
  output D,
  output EN,
  output CLK,
  output Q,
  output QN,
  output halt
);

  wire clock_1_out;
  wire [2:2] counter_1_q;

  Counter #(.width(3), .max('h7)) counter_1 (
    .Q({counter_1_q[2], D, CLK}), .carry(halt), .clk(clock_1_out));  // open: load, D, count, clr
  Clock clock_1 (.out(clock_1_out));
  D_flipflop d_flipflop_1 (.D(D), .EN(1'b1), .CLK(CLK), .Q(Q), .QN(QN));
  LED led_1 (.in(Q));
  LED led_2 (.in(QN));

  assign EN = 1'b1;

  // Notes on the sheet:
  //   顶层模块与自制子模块连接部分
  //   本地Logisim验证区域
  //   按Control+K触发执行，再次按Control+K暂停触发
endmodule

module D_latch (
  input  D,
  input  C,
  output Q,
  output QN
);


  // Notes on the sheet:
  //   D锁存器子模块实现区域
endmodule

module D_flipflop (
  input  D,
  input  EN,
  input  CLK,
  output Q,
  output QN
);


  // Notes on the sheet:
  //   D触发器子模块实现区域
endmodule
