// Logisim project exp2-1 译码器 - 作答区.circ as structural Verilog: 2 circuits, main circuit main
module main (
  output E0,
  output E1,
  output E2,
  output I0,
  output I1,
  output I2,
  output O0,
  output O1,
  output O2,
  output O3,
  output O4,
  output O5,
  output O6,
  output halt,
  output O7
);

  wire clock_1_out, pull_resistor_1_node;
  wire [2:0] priority_encoder_1_out;
  wire [3:0] bit_extender_1_out;
  wire [7:0] Y;

  Counter #(.width(6), .max('h3f), .behavior("old")) counter_1 (
    .Q({E2, E1, E0, I2, I1, I0}), .carry(halt), .clk(clock_1_out));  // open: load, D, count, clr, preset
  Clock clock_1 (.out(clock_1_out));
  _3_8_decoder u_3_8_decoder_1 (
    .G1(E0), .G2A_L(E1), .G2B_L(E2), .A(I0), .B(I1), .C(I2), .Y2_L(O2), .Y3_L(O3), .Y0_L(O0), .Y1_L(O1),
    .Y4_L(O4), .Y5_L(O5), .Y6_L(O6), .Y7_L(O7));
  assign Y = ~{O7, O6, O5, O4, O3, O2, O1, O0};  // NOT_Gate not_1, 8 bits wide
  Priority_Encoder priority_encoder_1 (
    .in0(Y[0]), .in1(Y[1]), .in2(Y[2]), .in3(Y[3]), .in4(Y[4]), .in5(Y[5]), .in6(Y[6]), .in7(Y[7]),
    .out(priority_encoder_1_out), .en_in(pull_resistor_1_node));  // open: gs, en_out
  Pull_Resistor #(.pull(1)) pull_resistor_1 (.node(pull_resistor_1_node));
  assign bit_extender_1_out = {{1{1'b0}}, priority_encoder_1_out};  // Bit_Extender bit_extender_1
  Hex_Digit_Display hex_digit_display_1 (.value(bit_extender_1_out));  // open: dp

  // Notes on the sheet:
  //   顶层模块与自制子模块连接部分
  //   本地Logisim验证区域
  //   按Control+K触发执行，再次按Control+K暂停触发
endmodule

// 3-8 Decoder
module _3_8_decoder (
  input  G1,
  input  G2A_L,
  input  G2B_L,
  input  A,
  input  B,
  input  C,
  output Y0_L,
  output Y1_L,
  output Y2_L,
  output Y3_L,
  output Y4_L,
  output Y5_L,
  output Y6_L,
  output Y7_L
);


  // Notes on the sheet:
  //   3-8译码器子模块实现区域
endmodule
