// Logisim project exp2-2 优先编码器 - 作答区.circ as structural Verilog: 2 circuits, main circuit main
module main (
  output I0,
  output I1,
  output I2,
  output I3,
  output I4,
  output I5,
  output I6,
  output I7,
  output O0,
  output O1,
  output O2,
  output halt
);

  wire clock_1_out;
  wire [3:0] bit_extender_1_out;

  Counter #(.behavior("old")) counter_1 (
    .Q({I7, I6, I5, I4, I3, I2, I1, I0}), .carry(halt), .clk(clock_1_out));  // open: load, D, count, clr, preset
  Clock clock_1 (.out(clock_1_out));
  _8_3_pri_encoder u_8_3_pri_encoder_1 (
    .I0(I0), .I1(I1), .O2(O2), .I2(I2), .I3(I3), .I4(I4), .I5(I5), .I6(I6), .I7(I7), .O1(O1), .O0(O0));
  assign bit_extender_1_out = {{1{1'b0}}, {O0, O1, O2}};  // Bit_Extender bit_extender_1
  Hex_Digit_Display hex_digit_display_1 (.value(bit_extender_1_out));  // open: dp

  // Other names for the same wires on the sheet: Y[2:0] = {O0, O1, O2}

  // Notes on the sheet:
  //   顶层模块与自制子模块连接部分
  //   本地Logisim验证区域
  //   按Control+K触发执行，再次按Control+K暂停触发
endmodule

// 8-3 PEncoder
module _8_3_pri_encoder (
  input  I0,
  input  I1,
  input  I2,
  input  I3,
  input  I4,
  input  I5,
  input  I6,
  input  I7,
  output O0,
  output O1,
  output O2
);


  // Notes on the sheet:
  //   8-3优先编码器子模块实现区域
endmodule
