// Logisim project realanswer.circ as structural Verilog: 2 circuits, main circuit main
module main (
  output I0,
  output I1,
  output I2,
  output I3,
  output I4,
  output I5,
  output I6,
  output I7,
  output O0,
  output O1,
  output O2,
  output halt
);

  wire clock_1_out;
  wire [3:0] bit_extender_1_out;

  Counter counter_1 (
    .Q({I7, I6, I5, I4, I3, I2, I1, I0}), .carry(halt), .clk(clock_1_out));  // open: load, D, count, clr
  Clock clock_1 (.out(clock_1_out));
  _8_3_pri_encoder u_8_3_pri_encoder_1 (
    .I0(I0), .I1(I1), .O2(O2), .I2(I2), .I3(I3), .I4(I4), .I5(I5), .I6(I6), .I7(I7), .O1(O1), .O0(O0));
  assign bit_extender_1_out = {{1{1'b0}}, {O0, O1, O2}};  // Bit_Extender bit_extender_1
  Hex_Digit_Display hex_digit_display_1 (.value(bit_extender_1_out));  // open: dp

  // Other names for the same wires on the sheet: Y[2:0] = {O0, O1, O2}

  // Notes on the sheet:
  //   顶层模块与自制子模块连接部分
  //   本地Logisim验证区域
  //   按Control+K触发执行，再次按Control+K暂停触发
endmodule

// 8-3 PEncoder
module _8_3_pri_encoder (
  input  I0,
  input  I1,
  input  I2,
  input  I3,
  input  I4,
  input  I5,
  input  I6,
  input  I7,
  output O0,
  output O1,
  output O2
);

  wire and_1_out, and_2_out, and_3_out, and_4_out, and_5_out, and_6_out, and_7_out, not_1_out, not_2_out,
       not_3_out, not_4_out, not_5_out, not_6_out, not_7_out, not_8_out, not_9_out, not_10_out, not_11_out,
       not_12_out, not_13_out, not_14_out, not_15_out, not_16_out, not_17_out, not_18_out, not_19_out,
       not_20_out, not_21_out, not_22_out, not_23_out, not_24_out, not_25_out, not_26_out, not_27_out,
       not_28_out;

  not not_1 (not_1_out, I0);
  not not_2 (not_2_out, I0);
  not not_3 (not_3_out, I1);
  not not_4 (not_4_out, I0);
  not not_5 (not_5_out, I1);
  not not_6 (not_6_out, I2);
  not not_7 (not_7_out, I0);
  not not_8 (not_8_out, I1);
  not not_9 (not_9_out, I2);
  not not_10 (not_10_out, I3);
  not not_11 (not_11_out, I0);
  not not_12 (not_12_out, I1);
  not not_13 (not_13_out, I2);
  not not_14 (not_14_out, I3);
  not not_15 (not_15_out, I4);
  not not_16 (not_16_out, I0);
  not not_17 (not_17_out, I1);
  not not_18 (not_18_out, I2);
  not not_19 (not_19_out, I3);
  not not_20 (not_20_out, I4);
  not not_21 (not_21_out, I5);
  not not_22 (not_22_out, I0);
  not not_23 (not_23_out, I1);
  not not_24 (not_24_out, I2);
  not not_25 (not_25_out, I3);
  not not_26 (not_26_out, I4);
  not not_27 (not_27_out, I5);
  not not_28 (not_28_out, I6);
  and and_1 (and_1_out, not_1_out, I1);
  and and_2 (and_2_out, not_2_out, not_3_out, I2);
  and and_3 (and_3_out, not_4_out, not_5_out, not_6_out, I3);
  and and_4 (and_4_out, not_7_out, not_8_out, not_9_out, not_10_out, I4);
  and and_5 (and_5_out, not_11_out, not_12_out, not_13_out, not_14_out, not_15_out, I5);
  and and_6 (and_6_out, not_16_out, not_17_out, not_18_out, not_19_out, not_20_out, not_21_out, I6);
  and and_7 (and_7_out, not_22_out, not_23_out, not_24_out, not_25_out, not_26_out, not_27_out, not_28_out, I7);
  or or_1 (O0, and_5_out, and_6_out, and_7_out, and_4_out);
  or or_2 (O1, and_2_out, and_3_out, and_6_out, and_7_out);
  or or_3 (O2, and_1_out, and_3_out, and_5_out, and_7_out);
endmodule
