// Logisim project 终于过了.circ as structural Verilog
module main (
  output [4:0] rd,
  output [4:0] rs1,
  output [4:0] rs2,
  output [6:0] funct7,
  output Branch,
  output Jump,
  output ALUAsrc,
  output [1:0] ALUBsrc,
  output [3:0] ALUctr,
  output MemtoReg,
  output RegWr,
  output MemWr,
  output halt,
  output [2:0] ExtOp
);

  wire clk;
  wire [2:0] \指令测试_1_funct3 ;
  wire [6:0] \指令测试_1_opcode ;
  wire [9:0] Addr;
  wire [11:0] bit_extender_1_out;
  wire [31:0] Instr;

  Clock clock_1 (.out(clk));
  Counter #(.width(4), .max('hf), .trigger("falling")) counter_1 (
    .carry(halt), .clk(clk));  // open: load, D, count, Q, clr
  \指令测试  \u_指令测试_1  (
    .CLK(clk), .Jump(Jump), .Branch(Branch), .Zero(1'b1), .opcode(\指令测试_1_opcode ), .rd(rd),
    .funct3(\指令测试_1_funct3 ), .rs1(rs1), .rs2(rs2), .funct7(funct7), .ExtOp(ExtOp), .instr(Instr),
    .instr_addr(Addr));  // open: imm
  assign bit_extender_1_out = {{2{1'b0}}, Addr};  // Bit_Extender bit_extender_1
  \控制器  \u_控制器_1  (
    .op0(\指令测试_1_opcode [0]), .Branch(Branch), .op1(\指令测试_1_opcode [1]), .op2(\指令测试_1_opcode [2]),
    .op3(\指令测试_1_opcode [3]), .Jump(Jump), .op4(\指令测试_1_opcode [4]), .op5(\指令测试_1_opcode [5]),
    .MemtoReg(MemtoReg), .op6(\指令测试_1_opcode [6]), .fn0(\指令测试_1_funct3 [0]), .fn1(\指令测试_1_funct3 [1]),
    .fn2(\指令测试_1_funct3 [2]), .RegWr(RegWr), .MemWr(MemWr), .ALUctr0(ALUctr[0]), .ALUctr1(ALUctr[1]),
    .ALUctr2(ALUctr[2]), .ALUctr3(ALUctr[3]), .ALUASrc(ALUAsrc), .ALUBSrc0(ALUBsrc[0]),
    .ALUBSrc1(ALUBsrc[1]), .ExtOP0(ExtOp[0]), .ExtOP1(ExtOp[1]), .ExtOP2(ExtOp[2]));
  Hex_Digit_Display hex_digit_display_1 (.value(Instr[31:28]));  // open: dp
  Hex_Digit_Display hex_digit_display_2 (.value(Instr[27:24]));  // open: dp
  Hex_Digit_Display hex_digit_display_3 (.value(Instr[19:16]));  // open: dp
  Hex_Digit_Display hex_digit_display_4 (.value(Instr[23:20]));  // open: dp
  Hex_Digit_Display hex_digit_display_5 (.value(Instr[15:12]));  // open: dp
  Hex_Digit_Display hex_digit_display_6 (.value(Instr[11:8]));  // open: dp
  Hex_Digit_Display hex_digit_display_7 (.value(bit_extender_1_out[11:8]));  // open: dp
  Hex_Digit_Display hex_digit_display_8 (.value(Instr[3:0]));  // open: dp
  Hex_Digit_Display hex_digit_display_9 (.value(Instr[7:4]));  // open: dp
  Hex_Digit_Display hex_digit_display_10 (.value(bit_extender_1_out[3:0]));  // open: dp
  Hex_Digit_Display hex_digit_display_11 (.value(bit_extender_1_out[7:4]));  // open: dp

  // Notes on the sheet:
  //   当前执行指令原码
  //   下条指令读取地址
  //   顶层模块与自制子模块连接部分
  //   本地Logisim验证区域
  //   按Control+K触发执行，再次按Control+K暂停触发
endmodule

module \指令存储器  (
  input  [9:0] Addr,
  output [31:0] Instr
);

  ROM #(.addrWidth(10), .dataWidth(32)) rom_1 (.addr(Addr), .data(Instr));  // open: sel

  // Notes on the sheet:
  //   指令存储器子模块实现区域
  //   contents of rom_1 (hex, n*v repeats v):
  //   a004b3 20af33 20bf33 f00ef13 412483 8137 912223 7ea500e3 1015*0 818ff56f
endmodule

module \立即数扩展器件  (
  input  [31:0] Instr,
  input  [2:0] ExtOp,
  output [31:0] Imm
);

  Multiplexer #(.select(3), .width(32), .enable("false")) multiplexer_1 (
    .in0({{20{1'b0}}, Instr[31:20]}), .in1({Instr[31:12], {12{1'b0}}}),
    .in2({{20{1'b0}}, Instr[31:25], Instr[11:7]}),
    .in3({{20{1'b0}}, Instr[7], Instr[30:25], Instr[11:8], 1'b0}),
    .in4({{12{1'b0}}, Instr[19:12], Instr[20], Instr[30:21], 1'b0}), .in5({32{1'b0}}), .in6({32{1'b0}}),
    .in7({32{1'b0}}), .out(Imm), .sel(ExtOp));

  // Notes on the sheet:
  //   立即数扩展器件子模块实现区域
endmodule

module \控制器  (
  input  op0,
  input  op1,
  input  op2,
  input  op3,
  input  op4,
  input  op5,
  input  op6,
  input  fn0,
  input  fn1,
  input  fn2,
  output Branch,
  output Jump,
  output MemtoReg,
  output RegWr,
  output MemWr,
  output ALUctr0,
  output ALUctr1,
  output ALUctr2,
  output ALUctr3,
  output ALUASrc,
  output ALUBSrc0,
  output ALUBSrc1,
  output ExtOP0,
  output ExtOP1,
  output ExtOP2
);

  wire and_1_out, and_2_out, and_3_out, and_4_out, and_5_out, and_6_out, and_7_out, and_8_out, and_9_out,
       and_10_out, and_11_out, and_12_out, and_13_out, not_1_out, not_2_out, not_3_out, not_4_out, not_5_out,
       not_6_out, not_7_out, not_8_out, not_9_out, not_10_out, not_11_out, not_12_out, not_13_out,
       not_14_out, not_15_out, not_16_out, not_17_out, not_18_out, not_19_out, not_20_out, not_21_out;

  not not_1 (not_1_out, op4);
  not not_2 (not_2_out, op6);
  not not_3 (not_3_out, op6);
  not not_4 (not_4_out, op6);
  and and_1 (and_1_out, op4, fn1);
  not not_5 (not_5_out, op6);
  not not_6 (not_6_out, op6);
  not not_7 (not_7_out, op6);
  not not_8 (not_8_out, op3);
  not not_9 (not_9_out, op6);
  not not_10 (not_10_out, op4);
  not not_11 (not_11_out, op6);
  not not_12 (not_12_out, op6);
  not not_13 (not_13_out, op6);
  not not_14 (not_14_out, op3);
  not not_15 (not_15_out, op6);
  not not_16 (not_16_out, op2);
  not not_17 (not_17_out, op4);
  not not_18 (not_18_out, op2);
  not not_19 (not_19_out, op5);
  not not_20 (not_20_out, fn2);
  not not_21 (not_21_out, op5);
  and and_2 (and_2_out, not_3_out, fn0);
  and and_3 (and_3_out, op2, not_4_out);
  and and_4 (and_4_out, op2, not_5_out);
  and and_5 (and_5_out, not_6_out, fn2);
  and and_6 (and_6_out, op2, not_7_out);
  and and_7 (and_7_out, not_8_out, op6);
  and and_8 (and_8_out, op2, not_9_out);
  and and_9 (and_9_out, not_10_out, not_11_out);
  and and_10 (and_10_out, not_12_out, fn2);
  and and_11 (and_11_out, op2, not_13_out);
  and and_12 (and_12_out, not_14_out, op6);
  and and_13 (and_13_out, op2, not_15_out);
  and and_14 (ExtOP1, not_16_out, not_17_out, op5);
  and and_15 (Branch, not_18_out, op6);
  and and_16 (MemtoReg, not_19_out, not_20_out);
  or or_1 (RegWr, not_21_out, op4, op3);
  and and_17 (MemWr, not_1_out, op5, not_2_out);
  or or_2 (ALUctr0, and_2_out, and_3_out);
  or or_3 (ALUctr1, and_1_out, and_4_out);
  or or_4 (ALUctr2, and_5_out, and_6_out);
  or or_5 (ALUctr3, and_7_out, and_8_out);
  or or_6 (ALUBSrc1, and_9_out, and_10_out, and_11_out);
  or or_7 (ExtOP0, and_12_out, and_13_out);

  assign ALUASrc = op3;
  assign ALUBSrc0 = op3;
  assign ExtOP2 = op3;
  assign Jump = op3;

  // Notes on the sheet:
  //   op6: pull=down
  //   fn0: pull=down
  //   fn2: pull=down
  //   op5: pull=down
  //   op0: pull=down
  //   op3: pull=down
  //   op4: pull=down
  //   fn1: pull=down
  //   op1: pull=down
  //   op2: pull=down
  //   控制器子模块实现区域
endmodule

module \指令测试  (
  input  CLK,
  input  Jump,
  input  Branch,
  input  Zero,
  input  [2:0] ExtOp,
  output [9:0] instr_addr,
  output [31:0] instr,
  output [6:0] opcode,
  output [4:0] rd,
  output [2:0] funct3,
  output [4:0] rs1,
  output [4:0] rs2,
  output [6:0] funct7,
  output [31:0] imm
);

  wire and_1_out, or_1_out;
  wire [31:0] adder_1_out, multiplexer_1_out, register_1_q;

  and and_1 (and_1_out, Branch, Zero);
  Register #(.width(32)) register_1 (
    .D(adder_1_out), .Q({register_1_q[31:12], instr_addr, register_1_q[1:0]}), .clk(CLK));  // open: en, clr
  or or_1 (or_1_out, Jump, and_1_out);
  Adder #(.width(32)) adder_1 (
    .a({register_1_q[31:12], instr_addr, register_1_q[1:0]}), .b(multiplexer_1_out), .out(adder_1_out));  // open: cin, cout
  Multiplexer #(.width(32), .enable("false")) multiplexer_1 (
    .in0(32'h4), .in1(imm), .out(multiplexer_1_out), .sel(or_1_out));
  \立即数扩展器件  \u_立即数扩展器件_1  (.Instr({funct7, instr[24:15], funct3, instr[11:0]}), .Imm(imm), .ExtOp(ExtOp));
  \指令存储器  \u_指令存储器_1  (.Addr(instr_addr), .Instr({funct7, instr[24:15], funct3, instr[11:0]}));

  assign {instr[31:25], instr[14:12]} = {funct7, funct3};
  assign opcode = instr[6:0];
  assign rd = instr[11:7];
  assign rs1 = instr[19:15];
  assign rs2 = instr[24:20];

  // Notes on the sheet:
  //   指令解析测试子模块实现区域
endmodule
