// Logisim project realanswer.circ as structural Verilog: 4 circuits, main circuit main
module main (
  output Cin,
  output [3:0] X,
  output [3:0] Y,
  output [3:0] S,
  output Cout,
  output halt
);

  wire [3:0] bit_extender_1_out, counter_1_q;

  Clock clock_1 (.out(Cin));
  Counter #(.width(4), .max('hf)) counter_1 (.Q(counter_1_q), .carry(halt), .clk(Cin));  // open: load, D, count, clr
  assign bit_extender_1_out = {{3{1'b0}}, Cin};  // Bit_Extender bit_extender_1
  Hex_Digit_Display hex_digit_display_1 (.value(bit_extender_1_out));  // open: dp
  ROM #(.addrWidth(4), .dataWidth(4)) rom_1 (.addr(counter_1_q), .data(Y));  // open: sel
  ROM #(.addrWidth(4), .dataWidth(4)) rom_2 (.addr(counter_1_q), .data(X));  // open: sel
  Hex_Digit_Display hex_digit_display_2 (.value(X));  // open: dp
  Hex_Digit_Display hex_digit_display_3 (.value(Y));  // open: dp
  Hex_Digit_Display hex_digit_display_4 (.value(S));  // open: dp
  \_4位CLA  \u_4位cla_1  (
    .X1(Y[0]), .S1(S[0]), .S2(S[1]), .S3(S[2]), .S4(S[3]), .Y1(X[0]), .X2(Y[1]), .Y2(X[1]), .X3(Y[2]),
    .Y3(X[2]), .X4(Y[3]), .Y4(X[3]), .Cin(Cin), .Cout(Cout));
  LED led_1 (.in(Cout));

  // Notes on the sheet:
  //   Cin
  //   contents of rom_1 (hex, n*v repeats v):
  //   0 1 2 3 4 5 6 7 8 9 a b c d e f
  //   contents of rom_2 (hex, n*v repeats v):
  //   a 0 1 2 3 a b c d f e d c 0 1 1
  //   X
  //   +
  //   +
  //   顶层模块与自制子模块连接部分
  //   本地Logisim验证区域
  //   按Control+K触发执行，再次按Control+K暂停触发
  //   Y
  //   =
  //   S
  //   Cout
endmodule

// FA
module \_1位全加器  (
  input  Cin,
  input  X,
  input  Y,
  output F,
  output P,
  output G
);

  wire xor_1_out;

  xor xor_1 (xor_1_out, X, Y);
  and and_1 (G, X, Y);
  or or_1 (P, X, Y);
  xor xor_2 (F, Cin, xor_1_out);

  // Notes on the sheet:
  //   1位全加法器子模块实现区域
endmodule

// 4-bit CLU
module \_4位CLU  (
  input  G4,
  input  P4,
  input  G3,
  input  P3,
  input  G2,
  input  P2,
  input  G1,
  input  P1,
  input  C0,
  output C4,
  output C3,
  output C2,
  output C1
);

  wire and_1_out, and_2_out, and_3_out, and_4_out, and_5_out, and_6_out, and_7_out, and_8_out, and_9_out,
       and_10_out;

  and and_1 (and_1_out, P4, G3);
  and and_2 (and_2_out, P4, P3, G2);
  and and_3 (and_3_out, P4, P3, P2, G1);
  and and_4 (and_4_out, P4, P3, P2, P1, C0);
  and and_5 (and_5_out, P3, G2);
  and and_6 (and_6_out, P3, P2, G1);
  and and_7 (and_7_out, P3, P2, P1, C0);
  and and_8 (and_8_out, P2, G1);
  and and_9 (and_9_out, P2, P1, C0);
  and and_10 (and_10_out, P1, C0);
  or or_1 (C4, G4, and_1_out, and_2_out, and_3_out, and_4_out);
  or or_2 (C3, G3, and_5_out, and_6_out, and_7_out);
  or or_3 (C2, G2, and_8_out, and_9_out);
  or or_4 (C1, G1, and_10_out);

  // Notes on the sheet:
  //   先行进位逻辑单元子模块实现区域
endmodule

// 4-bit CLA
module \_4位CLA  (
  input  Cin,
  input  X1,
  input  Y1,
  input  X2,
  input  Y2,
  input  X3,
  input  Y3,
  input  X4,
  input  Y4,
  output S1,
  output S2,
  output S3,
  output S4,
  output Cout
);

  wire \n1位全加器_1_g , \n1位全加器_1_p , \n1位全加器_2_g , \n1位全加器_2_p , \n1位全加器_3_g , \n1位全加器_3_p , \n1位全加器_4_g ,
       \n1位全加器_4_p , \n4位clu_1_c1 , \n4位clu_1_c2 , \n4位clu_1_c3 ;

  \_1位全加器  \u_1位全加器_1  (.Cin(Cin), .X(X1), .Y(Y1), .F(S1), .P(\n1位全加器_1_p ), .G(\n1位全加器_1_g ));
  \_1位全加器  \u_1位全加器_2  (.Cin(\n4位clu_1_c1 ), .X(X2), .Y(Y2), .F(S2), .P(\n1位全加器_2_p ), .G(\n1位全加器_2_g ));
  \_1位全加器  \u_1位全加器_3  (.Cin(\n4位clu_1_c2 ), .X(X3), .Y(Y3), .F(S3), .P(\n1位全加器_3_p ), .G(\n1位全加器_3_g ));
  \_1位全加器  \u_1位全加器_4  (.Cin(\n4位clu_1_c3 ), .X(X4), .Y(Y4), .F(S4), .P(\n1位全加器_4_p ), .G(\n1位全加器_4_g ));
  \_4位CLU  \u_4位clu_1  (
    .P1(\n1位全加器_1_p ), .C1(\n4位clu_1_c1 ), .C2(\n4位clu_1_c2 ), .G1(\n1位全加器_1_g ), .P2(\n1位全加器_2_p ),
    .G2(\n1位全加器_2_g ), .P3(\n1位全加器_3_p ), .G3(\n1位全加器_3_g ), .P4(\n1位全加器_4_p ), .G4(\n1位全加器_4_g ), .C0(Cin),
    .C3(\n4位clu_1_c3 ), .C4(Cout));

  // Notes on the sheet:
  //   先行进位加法器子模块实现区域
endmodule
